# Fritzing sketch schaltplan_bluetooth_prototyp (saved by Fritzing 0.9.3b)
breadboards: 1

parts:
  Bauteil2 = Bluetooth HC-05 Macho
  R1 = Resistor [tolerance=±5% resistance=1k package=THT]
  LED1 = LED - 5mm [color="Red (633nm)" package="5 mm [THT]"]
  R3 = Resistor [tolerance=±5% resistance=220 package=THT]
  Bauteil1 = Arduino Uno (Rev3) - ICSP
  R2 = Resistor [tolerance=±5% resistance=2k package=THT]

nets:
  N1: Bauteil2.TXD, R1.Pin_1
  N2: Bauteil2.RXD, Bauteil1.D0/RX
  VCC: Bauteil2.VCC, Bauteil1.5V
  GND: Bauteil2.GND, R3.Pin_0, Bauteil1.GND, R2.Pin_1
  N3: R1.Pin_0, Bauteil1.D1/TX, R2.Pin_0
  N4: LED1.cathode, R3.Pin_1
  N5: LED1.anode, Bauteil1.D7
